// Logisim project nr.circ as structural Verilog: 1 circuit, main circuit lab2
module lab2 (
  input  in_1,
  input  [7:0] Dividend_V,
  input  Clock,
  input  [7:0] Divisor_D,
  output out_5,
  output [7:0] Quotient,
  output [7:0] Remainder,
  output valid,
  output [7:0] Remainder_2,
  output [7:0] Quotient_2
);

  wire and_1_out, and_2_out, comparator_1_eq, comparator_1_gt, comparator_2_eq, comparator_4_lt,
       comparator_5_lt, not_1_out, not_2_out, not_3_out, shift_register_1_q7;
  wire [0:0] shifter_1_out_2;
  wire [7:0] adder_1_out, counter_1_q, multiplexer_1_out, multiplexer_2_out, Reg_U_q, Reg_V_q, shifter_2_out,
       subtractor_1_out;
  wire [7:1] shifter_1_out;

  and and_1 (and_1_out, not_2_out, Clock);
  Comparator comparator_1 (
    .a(multiplexer_2_out), .b({8{1'b0}}), .gt(comparator_1_gt), .eq(comparator_1_eq));  // open: lt
  or or_1 (Quotient_2[0], comparator_1_gt, comparator_1_eq);
  Adder adder_1 (.a({shifter_2_out[7:1], Reg_V_q[7]}), .b(Divisor_D), .out(adder_1_out), .cin(1'b0));  // open: cout
  Counter #(.trigger("falling")) counter_1 (
    .load(1'b0), .D({8{1'b0}}), .Q(counter_1_q), .clk(and_1_out), .clr(in_1));  // open: count, carry
  Multiplexer #(.width(8), .enable("false")) multiplexer_1 (
    .in0(Dividend_V), .in1({shifter_1_out, Quotient_2[0]}), .out(multiplexer_1_out), .sel(not_1_out));
  Multiplexer #(.width(8)) multiplexer_2 (
    .in0(subtractor_1_out), .in1(adder_1_out), .out(multiplexer_2_out), .sel(comparator_4_lt));  // open: en
  Comparator comparator_2 (.a(counter_1_q), .b(8'h1), .eq(comparator_2_eq));  // open: gt, lt
  Comparator comparator_3 (.a(counter_1_q), .b(8'h9), .eq(out_5));  // open: gt, lt
  not not_1 (not_1_out, comparator_2_eq);
  Register #(.trigger("falling")) Reg_V (.D(multiplexer_1_out), .Q(Reg_V_q), .clk(and_1_out));  // open: en, clr
  Register #(.trigger("falling")) Reg_U (.D(multiplexer_2_out), .Q(Reg_U_q), .clk(and_1_out));  // open: en, clr
  Subtractor subtractor_1 (
    .a({shifter_2_out[7:1], Reg_V_q[7]}), .b(Divisor_D), .out(subtractor_1_out), .bin(1'b0));  // open: bout
  not not_2 (not_2_out, out_5);
  Shifter shifter_1 (.in(Reg_V_q), .\dist (3'b001), .out({shifter_1_out, shifter_1_out_2[0]}));
  Shifter shifter_2 (.in(Reg_U_q), .\dist (3'b001), .out(shifter_2_out));
  not not_3 (not_3_out, out_5);
  Comparator comparator_4 (.a({shifter_2_out[7:1], Reg_V_q[7]}), .b({8{1'b0}}), .lt(comparator_4_lt));  // open: gt, eq
  Shift_Register #(.trigger("falling")) shift_register_1 (
    .shift(not_3_out), .in(Quotient_2[0]), .clk(and_1_out), .q0(Quotient_2[1]), .q1(Quotient_2[2]),
    .q2(Quotient_2[3]), .q3(Quotient_2[4]), .q4(Quotient_2[5]), .q5(Quotient_2[6]), .q6(Quotient_2[7]),
    .q7(shift_register_1_q7));  // open: out, load, clr, d0, d1, d2, d3, d4, d5, d6, d7
  Comparator comparator_5 (.a({shifter_2_out[7:1], Reg_V_q[7]}), .b({8{1'b0}}), .lt(comparator_5_lt));  // open: gt, eq
  Multiplexer #(.width(8)) multiplexer_3 (
    .in0({shifter_2_out[7:1], Reg_V_q[7]}), .in1(adder_1_out), .out(Remainder_2), .sel(and_2_out));  // open: en
  and and_2 (and_2_out, comparator_5_lt, out_5);

  // Notes on the sheet:
  //   q bit
  //   q
  //   Valid
endmodule
