// Logisim project r.circ as structural Verilog: 1 circuit, main circuit lab2
module lab2 (
  input  in_1,
  input  [7:0] Dividend_V,
  input  Clock,
  input  [7:0] Divisor_D,
  output [7:0] Quotient,
  output [7:0] Remainder,
  output valid,
  output [7:0] Remainder_2,
  output [7:0] Quotient_2
);

  wire and_1_out, comparator_1_eq, comparator_2_eq, not_2_out, not_3_out, not_4_out, shift_register_1_q7;
  wire [0:0] shifter_1_out_2, shifter_2_out;
  wire [6:0] Reg_V_q;
  wire [7:0] counter_1_q, multiplexer_1_out, multiplexer_2_out, Reg_U_q, subtractor_1_out;
  wire [7:1] shifter_1_out;

  and and_1 (and_1_out, not_3_out, Clock);
  not not_1 (Quotient_2[0], subtractor_1_out[7]);
  Counter #(.trigger("falling")) counter_1 (
    .load(1'b0), .D({8{1'b0}}), .Q(counter_1_q), .clk(and_1_out), .clr(in_1));  // open: count, carry
  Multiplexer #(.width(8), .enable("false")) multiplexer_1 (
    .in0(Dividend_V), .in1({shifter_1_out, Quotient_2[0]}), .out(multiplexer_1_out), .sel(not_2_out));
  Multiplexer #(.width(8)) multiplexer_2 (
    .in0(subtractor_1_out), .in1(Remainder_2), .out(multiplexer_2_out), .sel(subtractor_1_out[7]));  // open: en
  Comparator comparator_1 (.a(counter_1_q), .b(8'h1), .eq(comparator_1_eq));  // open: gt, lt
  Comparator comparator_2 (.a(counter_1_q), .b(8'h9), .eq(comparator_2_eq));  // open: gt, lt
  not not_2 (not_2_out, comparator_1_eq);
  Register #(.trigger("falling")) Reg_V (
    .D(multiplexer_1_out), .Q({Remainder_2[0], Reg_V_q}), .clk(and_1_out));  // open: en, clr
  Register #(.trigger("falling")) Reg_U (.D(multiplexer_2_out), .Q(Reg_U_q), .clk(and_1_out));  // open: en, clr
  Subtractor subtractor_1 (.a(Remainder_2), .b(Divisor_D), .out(subtractor_1_out), .bin(1'b0));  // open: bout
  not not_3 (not_3_out, comparator_2_eq);
  Shifter shifter_1 (.in({Remainder_2[0], Reg_V_q}), .\dist (3'b001), .out({shifter_1_out, shifter_1_out_2[0]}));
  Shifter shifter_2 (.in(Reg_U_q), .\dist (3'b001), .out({Remainder_2[7:1], shifter_2_out[0]}));
  not not_4 (not_4_out, comparator_2_eq);
  Shift_Register #(.trigger("falling")) shift_register_1 (
    .shift(not_4_out), .in(Quotient_2[0]), .clk(and_1_out), .q0(Quotient_2[1]), .q1(Quotient_2[2]),
    .q2(Quotient_2[3]), .q3(Quotient_2[4]), .q4(Quotient_2[5]), .q5(Quotient_2[6]), .q6(Quotient_2[7]),
    .q7(shift_register_1_q7));  // open: out, load, clr, d0, d1, d2, d3, d4, d5, d6, d7

  // Notes on the sheet:
  //   q bit
  //   q
  //   Valid
endmodule
